// Logisim project ALU.circ as structural Verilog: 19 circuits, main circuit ALU32
module LeftShift32 (
  input  [31:0] B,
  input  [4:0] Sa,
  input  Cin,
  output [31:0] C
);

  wire [31:0] leftshift1_1_c, leftshift2_1_c, leftshift4_1_c, leftshift8_1_c, leftshift16_1_c,
       multiplexer_1_out, multiplexer_2_out, multiplexer_3_out, multiplexer_4_out;

  Multiplexer #(.width(32), .enable("false")) multiplexer_1 (
    .in0(B), .in1(leftshift1_1_c), .out(multiplexer_1_out), .sel(Sa[0]));
  LeftShift1 leftshift1_1 (.B(B), .Cin(Cin), .C(leftshift1_1_c));
  LeftShift2 leftshift2_1 (.B(multiplexer_1_out), .Cin(Cin), .C(leftshift2_1_c));
  Multiplexer #(.width(32), .enable("false")) multiplexer_2 (
    .in0(multiplexer_1_out), .in1(leftshift2_1_c), .out(multiplexer_2_out), .sel(Sa[1]));
  LeftShift4 leftshift4_1 (.B(multiplexer_2_out), .Cin(Cin), .C(leftshift4_1_c));
  Multiplexer #(.width(32), .enable("false")) multiplexer_3 (
    .in0(multiplexer_2_out), .in1(leftshift4_1_c), .out(multiplexer_3_out), .sel(Sa[2]));
  Multiplexer #(.width(32), .enable("false")) multiplexer_4 (
    .in0(multiplexer_3_out), .in1(leftshift8_1_c), .out(multiplexer_4_out), .sel(Sa[3]));
  LeftShift8 leftshift8_1 (.B(multiplexer_3_out), .Cin(Cin), .C(leftshift8_1_c));
  LeftShift16 leftshift16_1 (.B(multiplexer_4_out), .Cin(Cin), .C(leftshift16_1_c));
  Multiplexer #(.width(32), .enable("false")) multiplexer_5 (
    .in0(multiplexer_4_out), .in1(leftshift16_1_c), .out(C), .sel(Sa[4]));

  // Notes on the sheet:
  //   LeftShift32
endmodule

module Add32 (
  input  [31:0] A,
  input  [31:0] B,
  input  Cin,
  output V,
  output [31:0] C
);

  wire add16_1_cout;

  Add16 add16_1 (.B(B[15:0]), .A(A[15:0]), .Cin(Cin), .Cout(add16_1_cout), .S(C[15:0]));  // open: V
  Add16 add16_2 (.B(B[31:16]), .A(A[31:16]), .Cin(add16_1_cout), .V(V), .S(C[31:16]));  // open: Cout

  // Notes on the sheet:
  //   32-bit Adder
endmodule

module ALU32 (
  input  [31:0] A,
  input  [31:0] B,
  input  [3:0] Op,
  input  [4:0] Sa,
  output V,
  output [31:0] C
);

  wire [31:0] addsub32_1_c, compare32_1_c, logicgate32_1_c, shift32_1_c;

  AddSub32 addsub32_1 (.A(A), .B(B), .Op(Op), .V(V), .C(addsub32_1_c));
  Compare32 compare32_1 (.A(A), .B(B), .Op(Op), .C(compare32_1_c));
  LogicGate32 logicgate32_1 (.A(A), .B(B), .Op(Op), .C(logicgate32_1_c));
  Shift32 shift32_1 (.B(B), .Op(Op), .Sa(Sa), .C(shift32_1_c));
  assign C = addsub32_1_c | compare32_1_c | logicgate32_1_c | shift32_1_c;  // OR_Gate or_1, 32 bits wide

  // Notes on the sheet:
  //   Overflow
  //   32-bit ALU
endmodule

module Add1 (
  input  A,
  input  B,
  input  Cin,
  output S,
  output Cout
);

  wire and_1_out, and_2_out, xor_1_out;

  xor xor_1 (xor_1_out, A, B);
  xor xor_2 (S, xor_1_out, Cin);
  and and_1 (and_1_out, xor_1_out, Cin);
  and and_2 (and_2_out, A, B);
  or or_1 (Cout, and_1_out, and_2_out);

  // Notes on the sheet:
  //   1-bit Full Adder
endmodule

module Add2 (
  input  [1:0] A,
  input  [1:0] B,
  input  Cin,
  output Cout,
  output V,
  output [1:0] S
);

  wire add1_1_cout;

  Add1 add1_1 (.Cout(add1_1_cout), .S(S[0]), .B(B[0]), .A(A[0]), .Cin(Cin));
  Add1 add1_2 (.Cout(Cout), .S(S[1]), .B(B[1]), .A(A[1]), .Cin(add1_1_cout));
  xor xor_1 (V, Cout, add1_1_cout);

  // Notes on the sheet:
  //   2-bit Adder
  //   Overflow: Cin msb != Cout msb
endmodule

module Add4 (
  input  [3:0] A,
  input  [3:0] B,
  input  Cin,
  output V,
  output Cout,
  output [3:0] S
);

  wire add2_1_cout;

  Add2 add2_1 (.A(A[1:0]), .Cout(add2_1_cout), .S(S[1:0]), .Cin(Cin), .B(B[1:0]));  // open: V
  Add2 add2_2 (.A(A[3:2]), .Cout(Cout), .S(S[3:2]), .V(V), .Cin(add2_1_cout), .B(B[3:2]));

  // Notes on the sheet:
  //   4-bit Adder
endmodule

module Add16 (
  input  [15:0] A,
  input  [15:0] B,
  input  Cin,
  output V,
  output Cout,
  output [15:0] S
);

  wire add8_1_cout;

  Add8 add8_1 (.B(B[7:0]), .A(A[7:0]), .Cin(Cin), .Cout(add8_1_cout), .S(S[7:0]));  // open: V
  Add8 add8_2 (.B(B[15:8]), .A(A[15:8]), .Cin(add8_1_cout), .V(V), .Cout(Cout), .S(S[15:8]));

  // Notes on the sheet:
  //   16-bit Adder
endmodule

module LeftShift1 (
  input  [31:0] B,
  input  Cin,
  output [31:0] C
);


  assign C = {B[30:0], Cin};

  // Notes on the sheet:
  //   1-bit shifter
endmodule

module LeftShift2 (
  input  [31:0] B,
  input  Cin,
  output [31:0] C
);

  assign C[1:0] = {{1{Cin}}, Cin};  // Bit_Extender bit_extender_1

  assign C[31:2] = B[29:0];

  // Notes on the sheet:
  //   2-bit shifter
endmodule

module LeftShift4 (
  input  [31:0] B,
  input  Cin,
  output [31:0] C
);

  assign C[3:0] = {{3{Cin}}, Cin};  // Bit_Extender bit_extender_1

  assign C[31:4] = B[27:0];

  // Notes on the sheet:
  //   4-bit shifter
endmodule

module LeftShift8 (
  input  [31:0] B,
  input  Cin,
  output [31:0] C
);

  assign C[7:0] = {{7{Cin}}, Cin};  // Bit_Extender bit_extender_1

  assign C[31:8] = B[23:0];

  // Notes on the sheet:
  //   8-bit shifter
endmodule

module LeftShift16 (
  input  [31:0] B,
  input  Cin,
  output [31:0] C
);

  assign C[15:0] = {{15{Cin}}, Cin};  // Bit_Extender bit_extender_1

  assign C[31:16] = B[15:0];

  // Notes on the sheet:
  //   16-bit shifter
endmodule

module BitReverser (
  input  [31:0] B,
  output [31:0] B_reversed,
  output sign
);


  assign B_reversed = {B[0], B[1], B[2], B[3], B[4], B[5], B[6], B[7], B[8], B[9], B[10], B[11], B[12], B[13], B[14], B[15], B[16], B[17], B[18], B[19], B[20], B[21], B[22], B[23], B[24], B[25], B[26], B[27], B[28], B[29], B[30], B[31]};
  assign sign = B[31];
endmodule

module Shift32 (
  input  [31:0] B,
  input  [3:0] Op,
  input  [4:0] Sa,
  output [31:0] C
);

  wire and_1_out, and_2_out, and_3_out, bitreverser_1_sign, xnor_1_out;
  wire [31:0] bitreverser_1_b_reversed, bitreverser_2_b_reversed, leftshift32_1_c, multiplexer_1_out;

  xnor xnor_1 (xnor_1_out, Op[2], Op[3]);
  Multiplexer #(.width(32), .enable("false")) multiplexer_1 (
    .in0(B), .in1(bitreverser_1_b_reversed), .out(multiplexer_1_out), .sel(Op[2]));
  BitReverser bitreverser_1 (.B(B), .B_reversed(bitreverser_1_b_reversed), .sign(bitreverser_1_sign));
  and and_1 (and_1_out, ~Op[1], xnor_1_out);  // AND_Gate
  and and_2 (and_2_out, bitreverser_1_sign, Op[2]);
  and and_3 (and_3_out, and_2_out, Op[0]);
  LeftShift32 leftshift32_1 (.B(multiplexer_1_out), .Sa(Sa), .Cin(and_3_out), .C(leftshift32_1_c));
  BitReverser bitreverser_2 (.B(leftshift32_1_c), .B_reversed(bitreverser_2_b_reversed));  // open: sign
  Multiplexer #(.width(32)) multiplexer_2 (
    .in0(leftshift32_1_c), .in1(bitreverser_2_b_reversed), .out(C), .sel(Op[2]), .en(and_1_out));

  // Notes on the sheet:
  //   Op3 == 1 ? right : left
  //   Op3 == Op2 and Op1 == 0
  //   sra ? signed : 0
  //   check active
  //   Shift Operator
  //   if shift right then reverse again
endmodule

module Add8 (
  input  [7:0] A,
  input  [7:0] B,
  input  Cin,
  output V,
  output Cout,
  output [7:0] S
);

  wire add4_1_cout;

  Add4 add4_1 (.A(A[3:0]), .S(S[3:0]), .Cout(add4_1_cout), .Cin(Cin), .B(B[3:0]));  // open: V
  Add4 add4_2 (.A(A[7:4]), .V(V), .S(S[7:4]), .Cout(Cout), .Cin(add4_1_cout), .B(B[7:4]));

  // Notes on the sheet:
  //   8-bit Adder
endmodule

module AddSub32 (
  input  [31:0] A,
  input  [31:0] B,
  input  [3:0] Op,
  output V,
  output [31:0] C
);

  wire add32_1_v, turnOn;
  wire [31:0] add32_1_c, bit_extender_1_out, bit_extender_2_out, xor_1_out;

  assign bit_extender_1_out = {{31{Op[2]}}, Op[2]};  // Bit_Extender bit_extender_1
  assign xor_1_out = B ^ bit_extender_1_out;  // XOR_Gate xor_1, 32 bits wide
  and and_1 (turnOn, Op[1], ~Op[3]);  // AND_Gate
  assign bit_extender_2_out = {{31{turnOn}}, turnOn};  // Bit_Extender bit_extender_2
  Add32 add32_1 (.A(A), .B(xor_1_out), .Cin(Op[2]), .V(add32_1_v), .C(add32_1_c));
  and and_2 (V, turnOn, add32_1_v);
  assign C = add32_1_c & bit_extender_2_out;  // AND_Gate and_3, 32 bits wide

  // Notes on the sheet:
  //   Op2 == 1? subtract: add
  //   Op3 == 0 and Op1= = 1
  //   check active
  //   Arithmetic Operator
  //   If not arithmetic operator => V = 0
  //   Overflow
endmodule

module Compare32 (
  input  [31:0] A,
  input  [31:0] B,
  input  [3:0] Op,
  output [31:0] C
);

  wire and_1_out, checkall0_1_all0, checkall0_2_all0, multiplexer_1_out, not_1_out, not_2_out, or_1_out,
       xnor_1_out;
  wire [31:0] xor_1_out;

  assign xor_1_out = B ^ A;  // XOR_Gate xor_1, 32 bits wide
  CheckAll0 checkall0_1 (.I(A), .All0(checkall0_1_all0));
  xnor xnor_1 (xnor_1_out, Op[1], Op[2]);
  CheckAll0 checkall0_2 (.I(xor_1_out), .All0(checkall0_2_all0));
  or or_1 (or_1_out, A[31], checkall0_1_all0);
  and and_1 (and_1_out, xnor_1_out, Op[3]);
  not not_1 (not_1_out, checkall0_2_all0);
  not not_2 (not_2_out, or_1_out);
  Multiplexer #(.select(2)) multiplexer_1 (
    .in0(not_1_out), .in1(checkall0_2_all0), .in2(or_1_out), .in3(not_2_out), .out(multiplexer_1_out),
    .sel(Op[1:0]), .en(and_1_out));
  assign C = {{31{1'b0}}, multiplexer_1_out};  // Bit_Extender bit_extender_1

  // Notes on the sheet:
  //   msb
  //   Op3 == 1 and Op1= = Op2
  //   if A==0 then le
  //   A!=B ? 1 :0
  //   A>0 ? 1:0
  //   check active
  //   Comparison Operator
endmodule

module CheckAll0 (
  input  [31:0] I,
  output All0
);

  nor nor_1 (All0, I[0], I[1], I[2], I[3], I[4], I[5], I[6], I[7], I[8], I[9], I[10], I[11], I[12], I[13], I[14], I[15], I[17], I[18], I[19], I[20], I[21], I[22], I[23], I[24], I[25], I[26], I[27], I[28], I[29], I[30], I[31], I[16]);

  // Notes on the sheet:
  //   Check if the input I == 0
endmodule

module LogicGate32 (
  input  [31:0] A,
  input  [31:0] B,
  input  [3:0] Op,
  output [31:0] C
);

  wire and_2_out, xnor_1_out, xor_2_out;
  wire [31:0] and_1_out, nor_1_out, or_1_out, xor_1_out;

  assign and_1_out = A & B;  // AND_Gate and_1, 32 bits wide
  assign or_1_out = A | B;  // OR_Gate or_1, 32 bits wide
  assign xor_1_out = A ^ B;  // XOR_Gate xor_1, 32 bits wide
  assign nor_1_out = ~(A | B);  // NOR_Gate nor_1, 32 bits wide
  xor xor_2 (xor_2_out, Op[2], Op[3]);
  xnor xnor_1 (xnor_1_out, Op[1], Op[3]);
  and and_2 (and_2_out, xor_2_out, xnor_1_out);
  Multiplexer #(.select(2), .width(32)) multiplexer_1 (
    .in0(and_1_out), .in1(or_1_out), .in2(xor_1_out), .in3(nor_1_out), .out(C), .sel(Op[1:0]), .en(and_2_out));

  // Notes on the sheet:
  //   Op2 != Op3 and Op1 == Op3
  //   Logical Operator
  //   check active
endmodule
